# Fritzing sketch Modul 1 L293D (saved by Fritzing 0.9.3b)
perfboards: 1

parts:
  L293D = L293D [package=THT]
  Part1 = Arduino Uno (Rev3)  # not connected
  J2 = Screw terminal - 2 pins [package=THT]
  VCC1 = Battery block 9V  # not connected
  J3 = Screw terminal - 2 pins [package=THT]  # not connected
  J4 = Screw terminal - 2 pins [package=THT]

nets:
  N1: L293D.Enable_1, L293D.+Vmotor, L293D.Enable_2, L293D.+V
  N2: L293D.Out_1_(_Controlled_by_Enable_1_), J4.pin1
  N3: L293D.Out_2_(_Controlled_by_Enable_1_), J4.pin2
  N4: L293D.Out_3_(_Controlled_by_Enable_2_), J2.pin1
  N5: L293D.Out_4_(_Controlled_by_Enable_2_), J2.pin2
